# Fritzing sketch sbr_v1.0 (saved by Fritzing 0.9.3b)
breadboards: 1

parts:
  J1 = STM32 Nucleo boards
  DC_Mot_Enc1 = DC Motor with two-phase hall-encoder [part_number=VT-E-G25A-06-177E]
  DC_Mot_Enc2 = DC Motor with two-phase hall-encoder [part_number=VT-E-G25A-06-177E]
  S1 = H-Bridge with L298N
  VCC1 = Battery block 9V
  GY2 = MPU-6050 Board GY-521 [form="♀ (female)" package=THT]
  S2 = Momentary Switch [package=ksa_sealed_tac_switch]
  LED1 = LED - 3mm [color="Red (633nm)" package="3 mm [THT]"]
  J2 = Piezo Speaker
  M1 = DOIT Esp32 DevKit v1 (30 pins long, 11 pins width) [part_number=ESP32S-PIN30]
  R1 = Resistor [tolerance=±5% resistance=220 package="2512 [SMD]"]

nets:
  N1: J1.PA11, S1.IN4
  N2: J1.E5V, DC_Mot_Enc1.pin4, DC_Mot_Enc2.pin4, S1.5V
  GND: J1.GND#333, DC_Mot_Enc1.pin3, DC_Mot_Enc2.pin3, S1.GND, VCC1.-, J2.pin1, M1.GND
  N3: J1.RESET, S2.3, M1.EN
  N4: J1.3v3, GY2.pin1
  N5: J1.GND#339, S2.1, R1.Pin_1
  N6: J1.IDD_01, J1.IDD_02
  N7: J1.CN_01, J1.CN_02
  N8: J1.CN_03, J1.CN_04
  N9: J1.JP5_2, J1.JP5_03
  N10: J1.GND#880, J1.GND#881
  N11: J1.GND#1149, J1.GND#1150
  N12: J1.PB8, GY2.pin3
  N13: J1.PB9, GY2.pin4
  N14: J1.PA5, LED1.anode
  N15: J1.PA6, DC_Mot_Enc1.pin6
  N16: J1.PA7, DC_Mot_Enc1.pin5
  N17: J1.PA9, S1.IN2
  N18: J1.PA8, S1.IN1
  N19: J1.PA10, S1.IN3
  N20: J1.GND#3310, GY2.pin2
  N21: J1.PA0, DC_Mot_Enc2.pin6
  N22: J1.PA1, DC_Mot_Enc2.pin5
  N23: J1.PB7, M1.TX0
  N24: DC_Mot_Enc1.pin1, S1.M2-01
  N25: DC_Mot_Enc1.pin2, S1.M2-02
  N26: DC_Mot_Enc2.pin1, S1.M1-02
  N27: DC_Mot_Enc2.pin2, S1.M1-01
  12V: S1.12V, VCC1.+, M1.VIN
  N28: S1.ENA, S1.ENA-5V
  N29: S1.ENB, S1.ENB-5V
  N30: LED1.cathode, R1.Pin_0
  N31: J2.pin2, M1.D23

custom parts:
  H-Bridge with L298N: h-bridge
  MPU-6050 Board GY-521: Acelerometro y Giroscopio MPU-6050 Board GY-521
  DOIT Esp32 DevKit v1 (30 pins long, 11 pins width): The DOIT Esp32 DevKit v1 is one of the development board created by DOIT to evaluate the ESP-WROOM-32 module. It is based on the ESP32 microcontroller that boasts Wifi, Bluetooth, Ethernet and Low Power support all in a single chip. (vanepp) made breadboard work, adjusted pin numbering and labels and reduced size of schematic and cleaned up pcb. This chip is 30pins long (2 x15) and 11 pins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
